// Logisim project logisim异或门和全加器.circ as structural Verilog: 1 circuit, main circuit main
module main (
  input  \本位A ,
  input  \输入A ,
  input  \本位B ,
  input  \输入B ,
  input  \进位C ,
  input  \输入A_2 ,
  input  \输入A_3 ,
  input  \输入B_2 ,
  input  \输入B_3 ,
  input  \输入A_4 ,
  input  \输入A_5 ,
  input  \输入B_4 ,
  input  \输入B_5 ,
  input  \输入A_6 ,
  input  \输入B_6 ,
  input  \输入A_7 ,
  input  \输入B_7 ,
  input  \进位C_2 ,
  output \本位输出 ,
  output \输出 ,
  output \进位输出 ,
  output \输出_2 ,
  output \输出_3 ,
  output \输出_4 ,
  output \输出_5 ,
  output \借用与门 ,
  output \输出_6 ,
  output \进位输出_2 ,
  output \本位输出_2 
);

  wire and_1_out, and_2_out, and_3_out, and_4_out, and_5_out, and_6_out, and_7_out, and_8_out, and_9_out,
       and_10_out, and_11_out, and_12_out, nand_1_out, nand_2_out, nand_3_out, nand_4_out, nand_5_out,
       nor_1_out, nor_2_out, nor_3_out, nor_4_out, nor_5_out, nor_6_out, nor_7_out, nor_8_out, nor_9_out,
       not_1_out, not_2_out, not_3_out, not_4_out, not_5_out, not_6_out, not_7_out, not_8_out, not_9_out,
       not_10_out, not_11_out, not_12_out, or_1_out, or_2_out, or_3_out, or_4_out, or_5_out, or_6_out,
       or_7_out, or_8_out, xor_1_out, xor_2_out;

  not not_1 (not_1_out, \输入A );
  not not_2 (not_2_out, \输入B );
  and and_1 (and_1_out, not_1_out, \输入B );
  and and_2 (and_2_out, \输入A , not_2_out);
  nand nand_1 (nand_1_out, \输入A_2 , \输入B_2 );
  not not_3 (not_3_out, \输入A_4 );
  and and_3 (and_3_out, \输入A_4 , \输入B_4 );
  not not_4 (not_4_out, \输入B_4 );
  not not_5 (not_5_out, \输入A_6 );
  and and_4 (and_4_out, \输入A_6 , \输入B_6 );
  not not_6 (not_6_out, \输入B_6 );
  not not_7 (not_7_out, \输入A_7 );
  and and_5 (and_5_out, \输入A_7 , \输入B_7 );
  not not_8 (not_8_out, \输入B_7 );
  and and_6 (and_6_out, \输入A_2 , nand_1_out);
  and and_7 (and_7_out, nand_1_out, \输入B_2 );
  nor nor_1 (nor_1_out, not_3_out, and_3_out);
  nor nor_2 (nor_2_out, and_3_out, not_4_out);
  nor nor_3 (nor_3_out, not_5_out, and_4_out);
  nor nor_4 (nor_4_out, and_4_out, not_6_out);
  nor nor_5 (nor_5_out, not_7_out, and_5_out);
  nor nor_6 (nor_6_out, and_5_out, not_8_out);
  or or_1 (or_1_out, and_1_out, and_2_out);
  or or_2 (or_2_out, and_6_out, and_7_out);
  or or_3 (or_3_out, nor_1_out, nor_2_out);
  or or_4 (or_4_out, nor_3_out, nor_4_out);
  or or_5 (or_5_out, nor_5_out, nor_6_out);
  not not_9 (not_9_out, or_5_out);
  and and_8 (and_8_out, or_5_out, \进位C_2 );
  not not_10 (not_10_out, \进位C_2 );
  nor nor_7 (nor_7_out, not_9_out, and_8_out);
  nor nor_8 (nor_8_out, and_8_out, not_10_out);
  xor xor_1 (xor_1_out, \本位A , \本位B );
  nand nand_2 (nand_2_out, \输入A_3 , \输入B_3 );
  not not_11 (not_11_out, \输入A_5 );
  not not_12 (not_12_out, \输入B_5 );
  or or_6 (or_6_out, and_5_out, and_8_out);
  or or_7 (or_7_out, nor_7_out, nor_8_out);
  nand nand_3 (nand_3_out, \输入A_3 , nand_2_out);
  nand nand_4 (nand_4_out, nand_2_out, \输入B_3 );
  and and_9 (and_9_out, \输入A_5 , \输入B_5 );
  and and_10 (and_10_out, not_11_out, not_12_out);
  xor xor_2 (xor_2_out, xor_1_out, \进位C );
  and and_11 (and_11_out, xor_1_out, \进位C );
  and and_12 (and_12_out, \本位A , \本位B );
  nand nand_5 (nand_5_out, nand_3_out, nand_4_out);
  nor nor_9 (nor_9_out, and_9_out, and_10_out);
  or or_8 (or_8_out, and_11_out, and_12_out);
endmodule
